// Logisim project lab2.circ as structural Verilog
module Secuencia_1 (
  input  X,
  input  in_2,
  output S
);

  wire clock_1_out, not_1_out, not_2_out, not_3_out, Q0, Q1, R0, S1;

  not not_1 (not_1_out, Q1);
  not not_2 (not_2_out, X);
  not not_3 (not_3_out, X);
  and and_1 (S, Q1, Q0, X);
  and and_2 (S1, not_1_out, Q0, not_2_out);
  and and_3 (R0, Q1, not_3_out);
  Clock clock_1 (.out(clock_1_out));
  S_R_Flip_Flop s_r_ff_1 (.S(S1), .clk(clock_1_out), .R(Q1), .Q(Q1), .reset(in_2));  // open: Qn, preset, en
  S_R_Flip_Flop s_r_ff_2 (.S(X), .clk(clock_1_out), .R(R0), .Q(Q0), .reset(in_2));  // open: Qn, preset, en

  // Other names for the same wires on the sheet: R1 = Q1; S0 = X
endmodule

module Secuencia_1_COPIA (
  input  Q1,
  input  Q0,
  input  X,
  output S1,
  output R1,
  output S0,
  output R0,
  output S
);

  wire not_1_out, not_2_out, not_3_out;

  not not_1 (not_1_out, Q1);
  not not_2 (not_2_out, X);
  not not_3 (not_3_out, X);
  and and_1 (S, Q1, Q0, X);
  and and_2 (S1, not_1_out, Q0, not_2_out);
  and and_3 (R0, Q1, not_3_out);

  assign R1 = Q1;
  assign S0 = X;
endmodule
